# Fritzing sketch boardLayout (saved by Fritzing 0.9.2b)
perfboards: 1

parts:
  JP1 = Header 10 [package=1x10-2mm-smd]
  JP4 = Header 10 [package=1x10-2mm-smd]
  JP5 = Header 10 [package=1x10-2mm-smd]
  JP6 = Header 10 [package=1x10-2mm-smd]  # not connected
  JP7 = Header 10 [package=1x10-2mm-smd]
  JP9 = Header 10 [package=1x10-2mm-smd]
  JP11 = Header 10 [package=1x10-2mm-smd]
  JP12 = Header 10 [package=1x10-2mm-smd]
  Part1 = Logic Level Converter
  JP13 = Header 10 [package=1x10-2mm-smd]
  JP14 = Header 10 [package=1x10-2mm-smd]  # not connected

nets:
  N1: JP1.1, JP7.7, JP11.10, JP12.10, Part1.LV
  N2: JP1.2, JP11.7
  N3: JP1.3, JP11.6, JP12.8
  N4: JP1.4, Part1.TX_LV
  N5: JP1.6, Part1.RX_LV
  N6: JP1.7, Part1.RX2_LV
  N7: JP1.8, Part1.TX2_LV
  N8: JP4.1, JP7.8
  N9: JP4.7, JP11.5, JP13.5
  N10: JP5.1, JP9.4, Part1.HV, JP13.10
  N11: JP5.4, JP11.9
  N12: JP5.5, JP11.8
  N13: JP5.9, JP7.10
  N14: JP5.10, JP7.9, JP9.3, Part1.GND
  N15: JP9.1, Part1.TX2_HV
  N16: JP9.2, Part1.RX2_HV
  N17: JP9.5, Part1.RX_HV
  N18: JP9.6, Part1.TX_HV
  N19: JP12.9, JP13.8
