# Fritzing sketch remoteBoard (saved by Fritzing 0.9.2b)
perfboards: 1

parts:
  U1 = SM130 [package=sm130]
  JP12 = Header 10 [package=1x10-2mm-smd]
  JP13 = Header 10 [package=1x10-2mm-smd]
  JP14 = Header 10 [package=1x10-2mm-smd]
  JP15 = Header 10 [package=1x10-2mm-smd]

nets:
  N1: U1.RX-I, JP15.3
  N2: U1.TX-O, JP15.4
  N3: JP12.6, JP12.8, JP12.10, JP13.7, JP14.7, JP15.9
  N4: JP13.8, JP15.5
  N5: JP13.9, JP15.6
  N6: JP13.10, JP15.2
  N7: JP14.8, JP15.8
  N8: JP14.9, JP15.7
  N9: JP14.10, JP15.1

notes:
  keypad
  display
